// Digital circuit 3AND.dig as structural Verilog
module _3AND (
  input  A,
  input  B,
  input  C,
  output Y
);

  wire and_1_out;

  and and_1 (and_1_out, A, B);
  and and_2 (Y, and_1_out, C);
endmodule
