// Digital circuit Abstracted_ALU.dig as structural Verilog
module Abstracted_ALU (
  input  A_1,
  input  A_0,
  input  B_1,
  input  B_0,
  input  [2:0] Control,
  input  Clk,
  output Y_1,
  output Y_0,
  output Carry,
  output Zero
);

  Two_Bit_ALU two_bit_alu_1 (
    .CTL(Control), .A_0(A_0), .A_1(A_1), .B_0(B_0), .B_1(B_1), .Clk(Clk), .Y_0(Y_0), .Y_1(Y_1), .Z(Zero),
    .C(Carry));

  // Notes on the sheet:
  //   The abstracted ALU
endmodule
