// Digital circuit Bitwise_AND.dig as structural Verilog
module Bitwise_AND (
  input  A_1,
  input  B_1,
  input  A_0,
  input  B_0,
  output Y_1,
  output Y_0
);

  and and_1 (Y_0, A_0, B_0);
  and and_2 (Y_1, A_1, B_1);

  // Notes on the sheet:
  //   Bitwise AND
endmodule
