// Digital circuit Neg_Edge_Triggered_D_FF.dig as structural Verilog
module Neg_Edge_Triggered_D_FF (
  input  D,
  input  Clk,
  output Q,
  output nQ
);

  wire d_ff_1_q, not_1_out;

  D_FF d_ff_1 (.D(D), .Clk(Clk), .Q(d_ff_1_q));  // open: nQ
  not not_1 (not_1_out, Clk);
  D_FF d_ff_2 (.D(d_ff_1_q), .Clk(not_1_out), .Q(Q), .nQ(nQ));

  // Notes on the sheet:
  //   Negative Edge Triggered D Flip Flop
endmodule
