// Digital circuit Parallel_Access_Shift_Register.dig as structural Verilog
module Parallel_Access_Shift_Register (
  input  Serial_Input,
  input  Shift_nLoad,
  input  Q_3,
  input  Q_2,
  input  Q_1,
  input  Q_0,
  input  Clk,
  output Q_3_2,
  output Q_2_2,
  output Q_1_2,
  output Q_0_2
);

  wire and_1_out, and_2_out, and_3_out, and_4_out, and_5_out, and_6_out, and_7_out, and_8_out, not_1_out,
       or_1_out, or_2_out, or_3_out, or_4_out;

  not not_1 (not_1_out, Shift_nLoad);
  and and_1 (and_1_out, Serial_Input, Shift_nLoad);
  and and_2 (and_2_out, not_1_out, Q_3);
  and and_3 (and_3_out, Q_3_2, Shift_nLoad);
  and and_4 (and_4_out, not_1_out, Q_2);
  and and_5 (and_5_out, Q_2_2, Shift_nLoad);
  and and_6 (and_6_out, not_1_out, Q_1);
  and and_7 (and_7_out, Q_1_2, Shift_nLoad);
  and and_8 (and_8_out, not_1_out, Q_0);
  or or_1 (or_1_out, and_1_out, and_2_out);
  or or_2 (or_2_out, and_3_out, and_4_out);
  or or_3 (or_3_out, and_5_out, and_6_out);
  or or_4 (or_4_out, and_7_out, and_8_out);
  D_FF d_ff_1 (.D(or_1_out), .C(Clk), .Q(Q_3_2));  // open: nQ
  D_FF d_ff_2 (.D(or_2_out), .C(Clk), .Q(Q_2_2));  // open: nQ
  D_FF d_ff_3 (.D(or_3_out), .C(Clk), .Q(Q_1_2));  // open: nQ
  D_FF d_ff_4 (.D(or_4_out), .C(Clk), .Q(Q_0_2));  // open: nQ
endmodule
