// Digital circuit Two_Bit_ALU.dig as structural Verilog
module Two_Bit_ALU (
  input  A_1,
  input  A_0,
  input  B_1,
  input  B_0,
  input  [2:0] CTL,
  input  Clk,
  output Y_0,
  output Y_1,
  output Z,
  output C
);

  wire bitwise_and_1_y_0, bitwise_and_1_y_1, bitwise_xor_1_y_0, bitwise_xor_1_y_1, two_bit_comparator_1_y_0,
       two_bit_comparator_1_y_1, two_bit_divider_1_y_0, two_bit_divider_1_y_1, two_bit_multiplier_1_m_0,
       two_bit_multiplier_1_m_1, two_bit_multiplier_1_m_2, two_bit_multiplier_1_m_3,
       two_bit_parallel_adder_1_c_out, two_bit_parallel_adder_1_s_0, two_bit_parallel_adder_1_s_1,
       two_bit_shift_left_1_y_0, two_bit_shift_left_1_y_1;

  Bitwise_AND bitwise_and_1 (
    .A_1(A_1), .B_1(B_1), .A_0(A_0), .B_0(B_0), .Y_1(bitwise_and_1_y_1), .Y_0(bitwise_and_1_y_0));
  Two_Bit_Parallel_Adder two_bit_parallel_adder_1 (
    .A_0(A_0), .B_0(B_0), .A_1(A_1), .B_1(B_1), .S_0(two_bit_parallel_adder_1_s_0),
    .S_1(two_bit_parallel_adder_1_s_1), .C_out(two_bit_parallel_adder_1_c_out));
  Two_Bit_Multiplier two_bit_multiplier_1 (
    .A_0(A_0), .A_1(A_1), .B_0(B_0), .B_1(B_1), .M_0(two_bit_multiplier_1_m_0),
    .M_1(two_bit_multiplier_1_m_1), .M_2(two_bit_multiplier_1_m_2), .M_3(two_bit_multiplier_1_m_3));
  Two_Bit_Divider two_bit_divider_1 (
    .A_0(A_0), .A_1(A_1), .B_0(B_0), .B_1(B_1), .Y_1(two_bit_divider_1_y_1), .Y_0(two_bit_divider_1_y_0));
  Two_Bit_Comparator two_bit_comparator_1 (
    .A_1(A_1), .B_1(B_1), .A_0(A_0), .B_0(B_0), .Y_0(two_bit_comparator_1_y_0), .Y_1(two_bit_comparator_1_y_1));
  Bitwise_XOR bitwise_xor_1 (
    .A_1(A_1), .B_1(B_1), .A_0(A_0), .B_0(B_0), .Y_1(bitwise_xor_1_y_1), .Y_0(bitwise_xor_1_y_0));
  Two_Bit_Shift_Left two_bit_shift_left_1 (
    .A_0(B_0), .A_1(B_1), .Clk(Clk), .Y_1(two_bit_shift_left_1_y_1), .Y_0(two_bit_shift_left_1_y_0));
  Multiplexer #(.Selector_Bits(3)) multiplexer_1 (
    .sel(CTL), .in_0(two_bit_parallel_adder_1_s_0), .in_1(two_bit_multiplier_1_m_0),
    .in_2(two_bit_divider_1_y_0), .in_3(two_bit_comparator_1_y_0), .in_4(bitwise_and_1_y_0),
    .in_5(bitwise_xor_1_y_0), .in_6(two_bit_shift_left_1_y_0), .in_7(1'b0), .out(Y_0));
  Multiplexer #(.Selector_Bits(3)) multiplexer_2 (
    .sel(CTL), .in_0(two_bit_parallel_adder_1_s_1), .in_1(two_bit_multiplier_1_m_1),
    .in_2(two_bit_divider_1_y_1), .in_3(two_bit_comparator_1_y_1), .in_4(bitwise_and_1_y_1),
    .in_5(bitwise_xor_1_y_1), .in_6(two_bit_shift_left_1_y_1), .in_7(1'b0), .out(Y_1));
  nor nor_1 (Z, Y_0, Y_1);
  _3OR _3or_1 (.A(two_bit_multiplier_1_m_2), .B(two_bit_parallel_adder_1_c_out), .C(two_bit_multiplier_1_m_3), .Y(C));

  // Notes on the sheet:
  //   Two Bit ALU
endmodule
