// Digital circuit Two_Bit_Comparator.dig as structural Verilog
module Two_Bit_Comparator (
  input  A_1,
  input  B_1,
  input  A_0,
  input  B_0,
  output Y_0,
  output Y_1
);

  wire and_1_out, and_2_out, and_3_out, and_4_out, and_5_out, and_6_out, and_7_out, nor_1_out, nor_2_out,
       not_1_out, not_2_out, not_3_out, not_4_out, or_1_out, or_2_out;

  not not_1 (not_1_out, A_1);
  not not_2 (not_2_out, B_1);
  not not_3 (not_3_out, A_0);
  and and_1 (and_1_out, not_1_out, B_1);
  and and_2 (and_2_out, A_1, not_2_out);
  and and_3 (and_3_out, not_3_out, B_0);
  and and_4 (and_4_out, A_0, not_4_out);
  not not_4 (not_4_out, B_0);
  nor nor_1 (nor_1_out, and_1_out, and_2_out);
  nor nor_2 (nor_2_out, and_3_out, and_4_out);
  and and_5 (and_5_out, nor_1_out, and_4_out);
  and and_6 (and_6_out, nor_1_out, and_3_out);
  and and_7 (and_7_out, nor_1_out, nor_2_out);
  or or_1 (or_1_out, and_2_out, and_5_out);
  or or_2 (or_2_out, and_1_out, and_6_out);
  or or_3 (Y_1, and_7_out, or_1_out);
  or or_4 (Y_0, and_7_out, or_2_out);

  // Notes on the sheet:
  //   A_1 < B_1
  //   A_1 > B_1
  //   A_0 < B_0
  //   A_0 > B_0
  //   A_1 = B_1
  //   A_0 = B_0
  //   A = B
  //   A > B
  //   A < B
endmodule
