// Digital circuit Two_Bit_Divider.dig as structural Verilog
module Two_Bit_Divider (
  input  A_0,
  input  A_1,
  input  B_0,
  input  B_1,
  output Y_1,
  output Y_0
);

  wire and_1_out, and_2_out, not_1_out, not_2_out, or_1_out;

  and and_1 (and_1_out, A_0, A_1);
  or or_1 (or_1_out, A_1, A_0);
  not not_1 (not_1_out, B_0);
  not not_2 (not_2_out, B_1);
  and and_2 (and_2_out, or_1_out, not_1_out);
  or or_2 (Y_0, and_1_out, and_2_out);
  and and_3 (Y_1, A_1, not_2_out);

  // Notes on the sheet:
  //   2-bit Divider
endmodule
