// Digital circuit Two_Bit_Multiplier.dig as structural Verilog
module Two_Bit_Multiplier (
  input  A_0,
  input  A_1,
  input  B_0,
  input  B_1,
  output M_0,
  output M_1,
  output M_2,
  output M_3
);

  wire and_2_out, and_3_out, and_4_out, and_5_out;

  and and_1 (M_0, A_0, B_0);
  and and_2 (and_2_out, A_1, B_1);
  and and_3 (and_3_out, A_0, B_1);
  and and_4 (and_4_out, A_1, B_1);
  and and_5 (and_5_out, and_2_out, and_3_out);
  xor xor_1 (M_1, and_2_out, and_3_out);
  xor xor_2 (M_2, and_5_out, and_4_out);
  and and_6 (M_3, and_4_out, and_5_out);
endmodule
