// Digital circuit Two_Bit_Parallel_Adder.dig as structural Verilog
module Two_Bit_Parallel_Adder (
  input  A_0,
  input  B_0,
  input  A_1,
  input  B_1,
  output S_0,
  output S_1,
  output C_out
);

  wire one_bit_full_adder_1_c_out;

  One_Bit_Full_Adder one_bit_full_adder_1 (
    .A(A_0), .B(B_0), .C_in(1'b0), .Sum(S_0), .C_out(one_bit_full_adder_1_c_out));
  One_Bit_Full_Adder one_bit_full_adder_2 (
    .A(A_1), .B(B_1), .C_in(one_bit_full_adder_1_c_out), .Sum(S_1), .C_out(C_out));
endmodule
