// Digital circuit Two_Bit_Shift_Left.dig as structural Verilog
module Two_Bit_Shift_Left (
  input  A_0,
  input  A_1,
  input  Clk,
  output Y_1,
  output Y_0
);

  wire and_1_out;

  and and_1 (and_1_out, 1'b0, A_1);
  D_FF d_ff_1 (.D(A_0), .C(~Clk), .Q(Y_1));  // open: nQ
  D_FF d_ff_2 (.D(and_1_out), .C(~Clk), .Q(Y_0));  // open: nQ

  // Notes on the sheet:
  //   Two Bit Shift Left Register
endmodule
